# Fritzing sketch Sketch04 (saved by Fritzing 0.9.3b)

parts:
  Mod2 = Microbit
  LED1 = LED - 3mm [color="Green (565nm)" package="3 mm [THT]"]
  LED2 = LED - 3mm [color="Green (565nm)" package="3 mm [THT]"]
  LED3 = LED - 3mm [color="Green (565nm)" package="3 mm [THT]"]
  LED4 = LED - 3mm [color="Green (565nm)" package="3 mm [THT]"]

nets:
  N1: Mod2.P0-bot, LED1.anode
  N2: Mod2.P1-bot, LED2.anode
  N3: Mod2.P8-bot, LED4.anode
  N4: Mod2.P2-bot, LED3.anode
  N5: Mod2.GND-18, LED1.cathode
  N6: LED2.cathode, LED3.cathode

custom parts:
  Microbit: BBC Microbit Fritzing part. July 2020 modify to match the xxx breakout board from yyyy. Remove pcb view as unused (this is a breakout board) and add all the connectors on the breakout board (not all of which I know the purpose of at the moment.)
