# Fritzing sketch Sketch06 (saved by Fritzing 0.9.3b)

parts:
  Mod2 = Microbit
  LED5 = RGB LED (com. cathode, rgb) [package="5 mm [THT]"]

nets:
  N1: Mod2.P0-bot, Mod2.3V3-bot, Mod2.p0-top, LED5.red_anode, LED5.common_cathode
  N2: Mod2.P1-bot, LED5.green_anode
  N3: Mod2.P2-bot, LED5.blue_anode

custom parts:
  Microbit: BBC Microbit Fritzing part. July 2020 modify to match the xxx breakout board from yyyy. Remove pcb view as unused (this is a breakout board) and add all the connectors on the breakout board (not all of which I know the purpose of at the moment.)
