# Fritzing sketch Sketch01 (saved by Fritzing 0.9.3b)

parts:
  RGB_SMD_LED1 = SMD RGB LED (WS2812B) [package=5050]
  RGB_SMD_LED2 = SMD RGB LED (WS2812B) [package=5050]
  RGB_SMD_LED3 = SMD RGB LED (WS2812B) [package=5050]
  RGB_SMD_LED4 = SMD RGB LED (WS2812B) [package=5050]
  Micro_bit1 = Microbit

nets:
  N1: RGB_SMD_LED1.DOUT, RGB_SMD_LED2.DIN
  N2: RGB_SMD_LED1.DIN, Micro_bit1.0
  N3: RGB_SMD_LED2.DOUT, RGB_SMD_LED3.DIN
  N4: RGB_SMD_LED3.DOUT, RGB_SMD_LED4.DIN

custom parts:
  SMD RGB LED (WS2812B): The WS2812B is an RGB LED with a WS2811 control IC built right into the LED. Its improvement over its WS2812 ancestor is the reduction to 4 pins (a single power supply instead of 2) and dropping the requirement for the external resistors. The manufacturer says it has a better reverse connect protection.
  Microbit: BBC Microbit Fritzing part
