# Fritzing sketch Sketch02 (saved by Fritzing 0.9.3b)

parts:
  Micro_bit1 = Microbit
  U1 = WS2812 RGB LED strip

nets:
  N1: Micro_bit1.0, U1.DIN

custom parts:
  Microbit: BBC Microbit Fritzing part
  WS2812 RGB LED strip: WS2812 strip
