# Fritzing sketch Sketch01 (saved by Fritzing 0.9.3b)

parts:
  Mod1 = Microbit
  Mod2 = Microbit

nets:
  N1: Mod1.P0-bot, Mod2.P1-bot, Mod2.P1-top
  N2: Mod1.P1-bot, Mod2.P0-bot, Mod2.p0-top
  N3: Mod1.GND-19, Mod1.GND-40, Mod2.GND-18, Mod2.GND-19

custom parts:
  Microbit: BBC Microbit Fritzing part. July 2020 modify to match the xxx breakout board from yyyy. Remove pcb view as unused (this is a breakout board) and add all the connectors on the breakout board (not all of which I know the purpose of at the moment.)
